# Fritzing sketch uart_2_uart_arduino_due (saved by Fritzing 0.9.0b)

parts:
  Composant1 = Bluetooth Mate Silver
  Composant2 = Arduino Due (Rev2b)

nets:
  N1: Composant1.RTS_5V, Composant1.RX_5V, Composant2.D18/TX1
  N2: Composant1.TX_5V, Composant2.D19/RX1
  N3: Composant1.VCC, Composant2.IOREF
  GND: Composant1.CTS_5V, Composant1.GND, Composant2.GND
