# Fritzing sketch uart_2_uart_arduino_mega2560 (saved by Fritzing 0.9.0b)

parts:
  Composant1 = Bluetooth Mate Silver
  Composant3 = Arduino Mega ADK (Rev3)

nets:
  N1: Composant1.RTS_5V, Composant1.RX_5V, Composant3.D18/TX1
  N2: Composant1.TX_5V, Composant3.D19/RX1
  VCC: Composant1.VCC, Composant3.3V3
  GND: Composant1.CTS_5V, Composant1.GND, Composant3.GND
